# Fritzing sketch main (saved by Fritzing 1.0.2b)
breadboards: 1

parts:
  Part1 = SparkFun Motor Driver TB6612FNG (v11) [part_number=ROB-14451]
  M2 = DC Motor [voltage_(max)=6V voltage_(min)=3V]
  VCC1 = Battery block 9V
  M3 = DC Motor [voltage_(max)=6V voltage_(min)=3V]
  S1 = Pushbutton [package="[THT]"]
  R1 = Resistor [tolerance=±5% power=0.25W resistance=220 package=THT]
  LED1 = LED - 5mm [color="Red (633nm)" current=0.030A package="5 mm [THT]"]
  A1 = mini560 [package=THT]
  U1 = ESP32S-HiLetgo [part_number=ESP32S-HiLetgo]
  Part2 = Analog Digital MUX Breakout
  S2 = Pololu QTR-8 Reflectabce Sensor array [package=THT]

nets:
  GND: Part1.GND, VCC1.-, LED1.cathode, A1.pin_4, A1.pin_6, A1.pin_7, U1.GND, Part2.GND, Part2.EN, S2.pin1, S2.pin15
  N1: Part1.B01, M3.pin_1
  N2: Part1.B02, M3.pin_2
  N3: Part1.A02, M2.pin_2
  N4: Part1.A01, M2.pin_1
  VCC: Part1.VCC, S1.Pin_3, S1.Pin_4, U1.3.3, Part2.VCC, S2.pin2, S2.pin13, S2.pin14, S2.pin23
  N5: Part1.VM, A1.pin_9, U1.VIN
  N6: Part1.PWMA, U1.GPIO23
  N7: Part1.AIN2, U1.GPIO18
  N8: Part1.AIN1, U1.GPIO19
  N9: Part1.STBY, U1.GPIO33
  N10: Part1.BIN1, U1.GPIO26
  N11: Part1.BIN2, U1.GPIO27
  N12: Part1.PWMB, U1.GPIO5
  N13: VCC1.+, A1.pin_1, A1.pin_2
  N14: S1.Pin_1, S1.Pin_2, U1.GPIO32
  N15: R1.Pin_0, U1.GPIO22
  N16: R1.Pin_1, LED1.anode
  N17: U1.GPIO25, Part2.SIG
  N18: U1.GPIO4, Part2.S3
  N19: U1.GPIO16, Part2.S2
  N20: U1.GPIO17, Part2.S1
  N21: U1.GPIO21, Part2.S0
  N22: Part2.C0, S2.pin12
  N23: Part2.C1, S2.pin11
  N24: Part2.C2, S2.pin10
  N25: Part2.C3, S2.pin9
  N26: Part2.C4, S2.pin8
  N27: Part2.C5, S2.pin7
  N28: Part2.C6, S2.pin4, S2.pin6
  N29: Part2.C7, S2.pin3, S2.pin5
  N30: S2.pin24, S2.pin25

custom parts:
  SparkFun Motor Driver TB6612FNG (v11): The TB6612FNG Motor Driver can control up to two DC motors at a constant current of 1.2A (3.2A peak). Two input signals (IN1 and IN2) can be used to control the motor in one of four function modes: CW, CCW, short-brake and stop. The two motor outputs (A and B) can be separately controlled, and the speed of each motor is controlled via a PWM input signal with a frequency up to 100kHz. The STBY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
  mini560: 5A DC-DC Mini 560 Step Down Stabilized Voltage Supply Module Output 3.3 5V 9V 12V Step-down Power Converter Board Module
  ESP32S-HiLetgo: HiLetgo ESP-WROOM-32 ESP32 ESP-32S Development Board 2.4GHz Dual-Mode WiFi + Bluetooth Dual Cores Microcontroller The ESP32 integrated with Antenna switches, RF Balun, power amplifiers, low-noise amplifiers, filters, and management modules, and the entire solution occupies the least area of PCB. 2.4 GHz Wi-Fi plus Bluetooth dual-mode chip, with TSMC Ultra-low power consumption 40nm technology,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
