# Fritzing sketch tema-6_transistores (saved by Fritzing 1.0.2b)
breadboards: 1

parts:
  U1 = ESP32S-HiLetgo [part_number=ESP32S-HiLetgo]
  U2 = POT [knob_status=50% power=0.5W package=pot_mammoth]
  R1 = Resistor [tolerance=±5% resistance=220 package="2512 [SMD]"]
  LED1 = LED - 3mm [color="Red (633nm)" current=0.030A package="3 mm [THT]"]
  R2 = Resistor [tolerance=±5% resistance=4.7k package="2512 [SMD]"]
  Q1 = Basic FET N-Channel [package="DPak [SMD]"]

nets:
  N1: U1.3.3, U2.E, R1.Pin_0
  N2: U1.GND, U2.S, Q1.source
  N3: U2.A, R2.Pin_1, Q1.Gate
  N4: R1.Pin_1, LED1.anode
  N5: LED1.cathode, R2.Pin_0

custom parts:
  ESP32S-HiLetgo: HiLetgo ESP-WROOM-32 ESP32 ESP-32S Development Board 2.4GHz Dual-Mode WiFi + Bluetooth Dual Cores Microcontroller The ESP32 integrated with Antenna switches, RF Balun, power amplifiers, low-noise amplifiers, filters, and management modules, and the entire solution occupies the least area of PCB. 2.4 GHz Wi-Fi plus Bluetooth dual-mode chip, with TSMC Ultra-low power consumption 40nm technology,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
