# Fritzing sketch tema-6_transistores_motor (saved by Fritzing 1.0.2b)
breadboards: 1

parts:
  U1 = ESP32S-HiLetgo [part_number=ESP32S-HiLetgo]
  Q1 = Basic FET N-Channel [package="DPak [SMD]"]
  S1 = Pushbutton [package="[SMD]"]
  R1 = Resistor [tolerance=±5% resistance=10k package="2512 [SMD]"]
  VCC1 = Battery block 9V
  D1 = Schottky Diode [part_number=1N5817 package="Melf DO-213 AB [SMD]"]
  M1 = DC Motor [voltage_(max)=6V voltage_(min)=3V]

nets:
  N1: U1.3.3, S1.Pin_3, S1.Pin_4
  N2: U1.GPIO32, S1.Pin_1, S1.Pin_2, R1.Pin_0
  N3: U1.GND, Q1.source, R1.Pin_1, VCC1.-
  N4: U1.GPIO22, Q1.Gate
  N5: Q1.drain, D1.anode, M1.pin_1
  N6: VCC1.+, D1.cathode, M1.pin_2

custom parts:
  ESP32S-HiLetgo: HiLetgo ESP-WROOM-32 ESP32 ESP-32S Development Board 2.4GHz Dual-Mode WiFi + Bluetooth Dual Cores Microcontroller The ESP32 integrated with Antenna switches, RF Balun, power amplifiers, low-noise amplifiers, filters, and management modules, and the entire solution occupies the least area of PCB. 2.4 GHz Wi-Fi plus Bluetooth dual-mode chip, with TSMC Ultra-low power consumption 40nm technology,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
