# Fritzing sketch tema-9 (saved by Fritzing 1.0.2b)
breadboards: 1

parts:
  U1 = ESP32S-HiLetgo [part_number=ESP32S-HiLetgo]
  S1 = Pololu QTR-8 Reflectabce Sensor array [package=THT]

nets:
  N1: U1.3.3, S1.pin2, S1.pin13, S1.pin22, S1.pin23
  N2: U1.GPIO32, S1.pin12
  N3: U1.GND, S1.pin1, S1.pin15
  N4: S1.pin24, S1.pin25

custom parts:
  ESP32S-HiLetgo: HiLetgo ESP-WROOM-32 ESP32 ESP-32S Development Board 2.4GHz Dual-Mode WiFi + Bluetooth Dual Cores Microcontroller The ESP32 integrated with Antenna switches, RF Balun, power amplifiers, low-noise amplifiers, filters, and management modules, and the entire solution occupies the least area of PCB. 2.4 GHz Wi-Fi plus Bluetooth dual-mode chip, with TSMC Ultra-low power consumption 40nm technology,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
